# Fritzing sketch esquema (saved by Fritzing 0.9.1b)
breadboards: 1

parts:
  Parte1 = Arduino Uno (Rev3)
  R1 = Trimmer Potentiometer [maximum_resistance=10kΩ package=THT]
  U1 = LCD-16X2 [package=lcd-16x2_nosilk]
  part = Resistor [tolerance=±5% resistance=330 package=THT]
  R3 = Resistor [tolerance=±5% resistance=10k package=THT]
  R4 = Photocell (LDR) [package=THT]
  RHT1 = Humidity and Temperature Sensor RHT03
  T1 = TMP36 Temperature Sensor [thermistor_type=NTC package="TO92 [THT]"]
  part_2 = Resistor [tolerance=±2% resistance=47k package=THT]

nets:
  N1: Parte1.A0, T1.Vout
  N2: Parte1.A5/SCL, R3.Pin_0, R4.pin_1
  N3: Parte1.D10_PWM/SS, U1.RS
  N4: Parte1.D11_PWM/MOSI, U1.E
  N5: Parte1.D12/MISO, RHT1.Data-signal, part_2.Pin_0
  N6: Parte1.D2, U1.DB4
  N7: Parte1.D3_PWM, U1.DB5
  N8: Parte1.D4, U1.DB6
  N9: Parte1.D5_PWM, U1.DB7
  5V: Parte1.5V, R1.leg2, U1.VDD, part.Pin_1, R4.pin_0, RHT1.Vcc, T1.+Vs, part_2.Pin_1
  GND: Parte1.GND, R1.leg1, U1.VSS, U1.R_W, U1.K, R3.Pin_1, RHT1.GND_2, T1.GND
  N10: R1.wiper, U1.VO
  N11: U1.A, part.Pin_0
